# Fritzing sketch connect-arduino (saved by Fritzing 0.9.3b)
breadboards: 1

parts:
  R1 = Resistor [tolerance=±20% resistance=330 package=THT]
  LED1 = LED - 5mm [color="Red (633nm)" package="5 mm [THT]"]
  Part1 = Arduino Uno (Rev3)
  R2 = Resistor [tolerance=±20% resistance=330 package=THT]
  LED2 = LED - 5mm [color="Blue (430nm)" package="5 mm [THT]"]
  R3 = Resistor [tolerance=±20% resistance=330 package=THT]
  LED3 = LED - 5mm [color="Green (555nm)" package="5 mm [THT]"]
  Part2 = LilyPad Buzzer
  S1 = Pushbutton [package="[THT]"]
  hc-sr1 = hc-sr04

nets:
  GND: R1.Pin_0, Part1.GND, R2.Pin_0, R3.Pin_0, Part2.-, S1.Pin_3, S1.Pin_4, hc-sr1.GND
  N1: R1.Pin_1, LED1.anode
  N2: LED1.cathode, Part1.D11_PWM/MOSI
  N3: Part1.D8, hc-sr1.Echo
  N4: Part1.D9_PWM, S1.Pin_1, S1.Pin_2
  N5: Part1.D10_PWM/SS, LED3.cathode
  N6: Part1.D12/MISO, LED2.cathode
  N7: Part1.D13/SCK, Part2.+
  N8: Part1.D6_PWM, hc-sr1.Trig
  5V: Part1.5V, hc-sr1.VCC
  N9: R2.Pin_1, LED2.anode
  N10: R3.Pin_1, LED3.anode
